# Fritzing sketch watermeter (saved by Fritzing 0.9.6b)
breadboards: 1

parts:
  WeMos_D1_Mini1 = WeMos D1 Mini
  LED1 = LED - 5mm [color="Red (633nm)" current=0.030 package="5 mm [THT]"]
  LED2 = LED - 5mm [color="Green (560nm)" current=0.030 package="5 mm [THT]"]
  Onderdeel1 = SHT1x-Breakout
  J1 = Dagu DGServo 9g header connector (female) [package=THT]  # not connected
  J2 = Piezo Speaker
  M1 = fc-51 [package=THT]

nets:
  N1: WeMos_D1_Mini1.D1, Onderdeel1.SCK
  N2: WeMos_D1_Mini1.D2, Onderdeel1.DATA
  N3: WeMos_D1_Mini1.D3, LED2.cathode
  N4: WeMos_D1_Mini1.D4, LED1.cathode
  N5: WeMos_D1_Mini1.D8, J2.pin2
  N6: LED1.anode, LED2.anode, Onderdeel1.GND, J2.pin1, M1.pin2
  N7: Onderdeel1.VCC, M1.pin3

notes:
  Bij gebrek aan een plaatje van een LJ18A3
  buzzer optioneel
  SHT kan ook HDC1080 zijn
